# Fritzing sketch Relay (saved by Fritzing 0.7.0b)
breadboards: 1

parts:
  K1 = Relay [part_number=FRS1B-S package=THT]
  Power_plug1 = Power plug
  R3 = Resistor [resistance=1k tolerance=±5% package=THT]
  Q2 = NPN-Transistor [package="TO92 [THT]"]
  D2 = Rectifier Diode [part_number=1N4001 package="300 mil [THT]"]
  M1 = DC Motor
  Arduino1 = Arduino

nets:
  N1: K1.A, M1.pin_1
  N2: K1.COIL1, Q2.C, D2.anode
  N3: K1.C1, K1.C2, Power_plug1.VCC
  N4: K1.COIL2, D2.cathode, Arduino1.+5V
  N5: Power_plug1.GND, M1.pin_2
  N6: R3.Pin_0, Q2.B
  N7: R3.Pin_1, Arduino1.D3
  N8: Q2.E, Arduino1.GND

notes:
  In this circuit a 5V relay is connected to the arduino board and controls a DC motor which is connected to an external power supply.
