# Fritzing sketch Shift_Register (saved by Fritzing 0.8.6b)
circuit board: 6.88566cm x 5.36311cm
breadboards: 2

parts:
  R10 = Resistor [resistance=220 tolerance=±5% package=THT]
  R11 = Resistor [resistance=220 tolerance=±5% package=THT]
  R12 = Resistor [resistance=220 tolerance=±5% package=THT]
  R13 = Resistor [resistance=220 tolerance=±5% package=THT]
  R14 = Resistor [resistance=220 tolerance=±5% package=THT]
  R15 = Resistor [resistance=220 tolerance=±5% package=THT]
  R16 = Resistor [resistance=220 tolerance=±5% package=THT]
  R17 = Resistor [resistance=220 tolerance=±5% package=THT]
  LED10 = LED - 5mm [color="Red (633nm)" package="5 mm [THT]"]
  LED11 = LED - 5mm [color="Red (633nm)" package="5 mm [THT]"]
  LED12 = LED - 5mm [color="Red (633nm)" package="5 mm [THT]"]
  LED13 = LED - 5mm [color="Red (633nm)" package="5 mm [THT]"]
  LED14 = LED - 5mm [color="Red (633nm)" package="5 mm [THT]"]
  LED15 = LED - 5mm [color="Red (633nm)" package="5 mm [THT]"]
  LED16 = LED - 5mm [color="Red (633nm)" package="5 mm [THT]"]
  LED17 = LED - 5mm [color="Red (633nm)" package="5 mm [THT]"]
  74HC5952 = 74HC595 [package="DIP16 [THT]"]
  C3 = Ceramic Capacitor [capacitance=100nF rated_voltage=35V package="200 mil [THT, multilayer]"]
  Arduino1 = Arduino Uno (Rev3)
  part = 74HC595 [package="DIP16 [THT]"]  # not connected

nets:
  N1: R10.Pin_0, LED14.anode
  N2: R10.Pin_1, 74HC5952.Q6
  N3: R11.Pin_0, LED10.anode
  N4: R11.Pin_1, 74HC5952.Q5
  N5: R12.Pin_0, LED12.anode
  N6: R12.Pin_1, 74HC5952.Q4
  N7: R13.Pin_0, LED11.anode
  N8: R13.Pin_1, 74HC5952.Q7
  N9: R14.Pin_0, LED13.anode
  N10: R14.Pin_1, 74HC5952.Q3
  N11: R15.Pin_0, LED15.anode
  N12: R15.Pin_1, 74HC5952.Q2
  N13: R16.Pin_0, LED16.anode
  N14: R16.Pin_1, 74HC5952.Q1
  N15: R17.Pin_0, LED17.anode
  N16: R17.Pin_1, 74HC5952.Q0
  GND: LED10.cathode, LED11.cathode, LED12.cathode, LED13.cathode, LED14.cathode, LED15.cathode, LED16.cathode, LED17.cathode, 74HC5952.GND, 74HC5952.OE, C3.1, Arduino1.GND
  VCC: 74HC5952.MR, 74HC5952.VCC, Arduino1.5V
  N17: 74HC5952.SH_CP, Arduino1.D12/MISO
  N18: 74HC5952.ST_CP, C3.0, Arduino1.D8
  N19: 74HC5952.DS, Arduino1.D11_PWM/MOSI

notes:
  In this project, a 74HC595 shift register is used to control 8 LEDs with just 3 Arduino pins.
  Related example: http://www.arduino.cc/en/Tutorial/ShiftOut
