# Fritzing sketch 555TouchSwitch (saved by Fritzing 0.8.5b)
circuit board: 6.88566cm x 5.36311cm
breadboards: 2

parts:
  Arduino1 = Arduino Uno (Rev3)
  C3 = Ceramic Capacitor [capacitance=100nF rated_voltage=35V package="200 mil [THT, multilayer]"]
  C4 = Ceramic Capacitor [capacitance=100nF rated_voltage=35V package="200 mil [THT, multilayer]"]
  R2 = Resistor [resistance=100k tolerance=±5% package=THT]
  U2 = 555 Timer [package="DIP8 [THT]"]
  TouchSwitch1 = Antenna

nets:
  N1: Arduino1.5V, R2.Pin_1, U2.Reset, U2.Vcc_Supply_Voltage
  N2: Arduino1.GND, C3.0, C4.1, U2.Ground
  N3: Arduino1.D6_PWM, U2.Output
  N4: C3.1, R2.Pin_0, U2.Threshold, U2.Discharge
  N5: C4.0, U2.Control_Voltage
  N6: U2.Trigger, TouchSwitch1.antenna_lead

notes:
  This is a 555 timer touch switch circuit based on a Forrest Mims circuit. The yellow wire serves as the touch sensor. Pin 3 on the 555 timer is the output signal and is read by Pin 6 on the Arduino.
  http://talkingelectronics.com/projects/TouchSwitch/TouchSwitch-1.html
