# Fritzing sketch Countdown (saved by Fritzing 0.7.0b)
breadboards: 1

parts:
  Segment1 = 7 Segment Display
  Segment2 = 7 Segment Display
  Q1 = NPN-Transistor [package="TO92 [THT]"]
  Q2 = PNP-Transistor [package="TO92 [THT]"]
  R1 = Resistor [tolerance=±5% resistance=1k package=THT]
  R2 = Resistor [tolerance=±5% resistance=1k package=THT]
  Q3 = PNP-Transistor [package="TO92 [THT]"]
  Q4 = NPN-Transistor [package="TO92 [THT]"]
  R3 = Resistor [tolerance=±5% resistance=1k package=THT]
  R4 = Resistor [tolerance=±5% resistance=1k package=THT]
  RE1 = Rotary Encoder [package=THT]
  S1 = Pushbutton [package="[THT]"]
  R5 = Resistor [tolerance=±5% resistance=10k package=THT]
  Arduino1 = Arduino

nets:
  N1: Segment1.Segment_E, Segment2.Segment_E, Arduino1.D12
  N2: Segment1.Segment_D, Segment2.Segment_D, Arduino1.D11
  N3: Segment1.common_anode, Q2.C
  N4: Segment1.Segment_C, Segment2.Segment_C, Arduino1.D9
  N5: Segment1.Segment_DP, Segment2.Segment_DP, Arduino1.D8
  N6: Segment1.Segment_B, Segment2.Segment_B, Arduino1.D3
  N7: Segment1.Segment_A, Segment2.Segment_A, Arduino1.D4
  N8: Segment1.Segment_F, Segment2.Segment_F, Arduino1.D5
  N9: Segment1.Segment_G, Segment2.Segment_G, Arduino1.D6
  N10: Segment2.common_anode, Q3.C
  N11: Q1.E, Q4.E, RE1.EncoderPinC, R5.Pin_0, Arduino1.GND
  N12: Q1.B, R1.Pin_0
  N13: Q1.C, R2.Pin_0
  N14: Q2.E, Q3.E, S1.Pin_1, S1.Pin_2, Arduino1.+5V
  N15: Q2.B, R2.Pin_1
  N16: R1.Pin_1, Arduino1.D10
  N17: Q3.B, R4.Pin_1
  N18: Q4.B, R3.Pin_1
  N19: Q4.C, R4.Pin_0
  N20: R3.Pin_0, Arduino1.D7
  N21: RE1.EncoderPinA, Arduino1.A1
  N22: RE1.EncoderPinB, Arduino1.A0
  N23: S1.Pin_3, S1.Pin_4, R5.Pin_1, Arduino1.D2

// code stored in the sketch: Countdown.ino
/*

inspired by circuits at home
http://www.circuitsathome.com/mcu/reading-rotary-encoder-on-arduino

*/

#define encPinA 14                           // rotary encoder pin A
int encALast;
#define encPinB 15                           // rotary encoder pin B

int theNumber = 0; // 3.8.2011
int val; 
int segments[7] = {3,4,9,11,12,5,6};       // pins, the segments are attached to
int digits[2] = {10,7};                    // common anode of each digit
int buttonPin = 2;                         // pin, where the start stop button is connected
int lastButtonState;

boolean timer = false;
long myStartTime;

long theSecond = 1000;

byte seven_seg_segments[10][7] = { 
  {1,1,1,1,1,1,0},  // = 0
  {0,1,1,0,0,0,0},  // = 1
  {1,1,0,1,1,0,1},  // = 2
  {1,1,1,1,0,0,1},  // = 3
  {0,1,1,0,0,1,1},  // = 4
  {1,0,1,1,0,1,1},  // = 5
  {1,0,1,1,1,1,1},  // = 6
  {1,1,1,0,0,0,0},  // = 7
  {1,1,1,1,1,1,1},  // = 8
  {1,1,1,0,0,1,1}   // = 9
};

void setup() {    
//  Serial.begin(9600);                    // starts serial communication
  pinMode(encPinA, INPUT);                    // set rotary encoder A pin as input
  pinMode(encPinB, INPUT);                    // set rotary encoder B pin as input  
  digitalWrite(encPinA, HIGH);                // switches internal drop down resistors on
  digitalWrite(encPinB, HIGH);                // switches internal drop down resistors on

  pinMode(buttonPin,INPUT);

  for (int i=0; i<7; i++){
    pinMode(segments[i], OUTPUT);           // sets the seven segment outputs
  }

  for (int i=0; i<2; i++){
    pinMode(digits[i], OUTPUT);             // sets the seven segment outputs 
  }
}

void sevenSegWrite(int thePosition, int digit) {  // write a number to a seven segment digit
  for (int i = 0; i < 7; i++) {          
    if (seven_seg_segments[digit][i] == 1){  
      digitalWrite(segments[i], LOW);
    } 
    else {
      digitalWrite(segments[i], HIGH);
    }
  }
  digitalWrite(digits[thePosition], HIGH);
  delayMicroseconds(200);
  digitalWrite(digits[thePosition], LOW);
  delayMicroseconds(200);
}

void clearDisplay() {                              // clear the display
  for (int i=0; i<5; i++){
    digitalWrite(digits[i], LOW);
  }
}

void showNumber(){                                 // show the number
  for (int stelle=0; stelle<2; stelle++){
    char szZahl[2];
    sprintf(szZahl, "%d", theNumber);
    int stellen = strlen(szZahl);
    if (stelle > stellen) {
    } 
    else {
      int ergebnis = szZahl[stelle] - '0';
      if (ergebnis>-1){
        sevenSegWrite((1-(stellen-(stelle+1))),ergebnis);
        delayMicroseconds(10);
      } 
      else {
        sevenSegWrite((1-(stellen-(stelle+1))),0);
        delayMicroseconds(10);
      }
    }
    delay(1);
    clearDisplay();
  }
}

void loop() {
  // read rotary encoder
  if (encALast!=digitalRead(encPinA)){
    if ((digitalRead(encPinA)==LOW)&&(digitalRead(encPinB)==LOW)) theNumber++;
    if ((digitalRead(encPinA)==LOW)&&(digitalRead(encPinB)==HIGH)) theNumber--;
  }
  
  
  encALast=digitalRead(encPinA);
  
  if (lastButtonState!=digitalRead(buttonPin)){
    if (digitalRead(buttonPin)==HIGH){
     timer?timer=false:timer=true;
     myStartTime=long(millis());
    }
  }
  lastButtonState=digitalRead(buttonPin);

  if (timer==true){
   if (long(millis())-myStartTime>1000){
     myStartTime=long(millis());
     theNumber--;
     if (theNumber==0){
       for (int i=0; i<5; i++){     
        for (int i=0; i<50; i++){ 
          showNumber();       
          delay(1);
        }
        clearDisplay();
        delay(100);  
       }
     }
   }
  } 
  
  if (theNumber>99) theNumber=0;
  if (theNumber<0) {
    theNumber=0;
    timer=false;
  }
  
  clearDisplay();
  showNumber();
}
