# Fritzing sketch Blink (saved by Fritzing 0.8.6b)
circuit board: 6.88566cm x 5.36311cm

parts:
  LED = LED - 5mm [color="Red (633nm)" package="5 mm [THT]"]
  Arduino1 = Arduino Uno (Rev3)
  part = LED - 5mm [color="Red (633nm)" package="5 mm [THT]"]  # not connected

nets:
  N1: LED.cathode, Arduino1.GND
  N2: LED.anode, Arduino1.D13/SCK

notes:
  BLINK
