# Fritzing sketch Servo (saved by Fritzing 0.8.6b)
circuit board: 6.88566cm x 5.36311cm
breadboards: 2

parts:
  Servo = Basic Servo
  Potentiometer = Rotary Potentiometer (Small) [maximum_resistance=100kΩ package=THT]
  Bauteil1 = Arduino Uno (Rev3)

nets:
  GND: Servo.gnd, Potentiometer.leg1, Bauteil1.GND
  VCC: Servo.vcc, Potentiometer.leg2, Bauteil1.5V
  N1: Servo.pulse, Bauteil1.D9_PWM
  N2: Potentiometer.wiper, Bauteil1.A0

notes:
  Orange
  Rot
  Braun
  SERVO
