# Fritzing sketch Verstaerkung (saved by Fritzing 0.8.4b)
circuit board: 6.88566cm x 5.36311cm
breadboards: 2

parts:
  Motor = DC Motor
  Batterie = Battery block 9V
  Arduino1 = Arduino Uno (Rev3)
  FET = Basic FET N-Channel [package="TO220 [THT]"]

nets:
  N1: Motor.pin_1, FET.drain
  N2: Motor.pin_2, Batterie.+
  N3: Batterie.-, Arduino1.GND, FET.source
  N4: Arduino1.D9_PWM, FET.gate

notes:
  +
  -
  VERSTAERKUNG
