# Fritzing sketch Fading (saved by Fritzing 0.8.6b)
circuit board: 6.88566cm x 5.36311cm
breadboards: 2

parts:
  R1 = Resistor [tolerance=±5% resistance=220 package=THT]
  LED1 = LED - 5mm [color="Red (633nm)" package="5 mm [THT]"]
  Bauteil1 = Arduino Uno (Rev3)
  part = LED - 5mm [color="Red (633nm)" package="5 mm [THT]"]  # not connected

nets:
  N1: R1.Pin_0, Bauteil1.D9_PWM
  N2: R1.Pin_1, LED1.anode
  N3: LED1.cathode, Bauteil1.GND

notes:
  FADING
