# Fritzing sketch Fortuneteller (saved by Fritzing 0.8.4b)
circuit board: 6.88566cm x 5.36311cm
breadboards: 2

parts:
  R1 = Resistor [tolerance=±5% resistance=100k package=THT]
  Tilt = Tilt Switch [package=THT]
  Arduino1 = Arduino Uno (Rev3)
  Warte_noch_etwas_damit = LED - 5mm [color="Yellow (585nm)" package="5 mm [THT]"]
  R4 = Resistor [tolerance=±5% resistance=220 package=THT]
  Ja_aber_mit_Stil! = LED - 5mm [color="Blue (505nm)" package="5 mm [THT]"]
  Nein_lieber_nicht = LED - 5mm [color="Red (633nm)" package="5 mm [THT]"]
  R5 = Resistor [tolerance=±5% resistance=220 package=THT]
  R6 = Resistor [tolerance=±5% resistance=220 package=THT]
  R2 = Resistor [tolerance=±5% resistance=220 package=THT]
  Folge_deinem_Herzen = LED - 5mm [color="Green (555nm)" package="5 mm [THT]"]
  R3 = Resistor [tolerance=±5% resistance=220 package=THT]
  Unbedingt!_Sofort! = LED - 5mm [color="Blue (505nm)" package="5 mm [THT]"]

nets:
  N1: R1.Pin_0, Tilt.Pin_2, Arduino1.D3_PWM
  N2: R1.Pin_1, Arduino1.5V
  N3: Tilt.Pin_1, Arduino1.GND, Warte_noch_etwas_damit.cathode, Ja_aber_mit_Stil!.cathode, Nein_lieber_nicht.cathode, Folge_deinem_Herzen.cathode, Unbedingt!_Sofort!.cathode
  N4: Arduino1.D8, R6.Pin_1
  N5: Arduino1.D9_PWM, R5.Pin_1
  N6: Arduino1.D10_PWM/SS, R4.Pin_1
  N7: Arduino1.D11_PWM/MOSI, R3.Pin_1
  N8: Arduino1.D12/MISO, R2.Pin_1
  N9: Warte_noch_etwas_damit.anode, R5.Pin_0
  N10: R4.Pin_0, Folge_deinem_Herzen.anode
  N11: Ja_aber_mit_Stil!.anode, R2.Pin_0
  N12: Nein_lieber_nicht.anode, R3.Pin_0
  N13: R6.Pin_0, Unbedingt!_Sofort!.anode

notes:
  FORTUNETELLER
