# Fritzing sketch Synthesizer (saved by Fritzing 0.8.4b)
circuit board: 6.88566cm x 5.36311cm
breadboards: 2

parts:
  R3 = Resistor [tolerance=±5% resistance=220 package=THT]
  Arduino1 = Arduino Uno (Rev3)
  SG1 = Buzzer 12mm [package=buzzer-12mm-ns]
  R1 = Rotary Potentiometer (Small) [maximum_resistance=100kΩ package=THT]
  R2 = Rotary Potentiometer (Small) [maximum_resistance=100kΩ package=THT]

nets:
  N1: R3.Pin_0, SG1.1
  N2: R3.Pin_1, Arduino1.GND, R1.leg1, R2.leg1
  N3: Arduino1.A0, R2.wiper
  N4: Arduino1.A1, R1.wiper
  N5: Arduino1.5V, R1.leg2, R2.leg2
  N6: Arduino1.D8, SG1.2

notes:
  SYNTHESIZER

custom parts:
  Buzzer 12mm: Buzzer 12mm Spark Fun Electronics SKU : Comp-Buzzer
