# Fritzing sketch LED-Matrix (saved by Fritzing 0.8.5b)
circuit board: 6.88566cm x 5.36311cm
breadboards: 2

parts:
  Arduino1 = Arduino Uno (Rev3)
  Q6 = PNP-Transistor [package="TO92 [THT]"]
  Q7 = PNP-Transistor [package="TO92 [THT]"]
  Q8 = PNP-Transistor [package="TO92 [THT]"]
  Q9 = PNP-Transistor [package="TO92 [THT]"]
  Q10 = PNP-Transistor [package="TO92 [THT]"]
  R6 = Resistor [tolerance=±5% resistance=1k package=THT]
  R7 = Resistor [tolerance=±5% resistance=1k package=THT]
  R8 = Resistor [tolerance=±5% resistance=1k package=THT]
  R9 = Resistor [tolerance=±5% resistance=1k package=THT]
  R10 = Resistor [tolerance=±5% resistance=1k package=THT]
  Dot_Matrix1 = LED Dot Matrix 18mm (0.7 INCH)

nets:
  N1: Arduino1.D8, R9.Pin_0
  N2: Arduino1.D9_PWM, Dot_Matrix1.Row_4
  N3: Arduino1.D10_PWM/SS, R10.Pin_0
  N4: Arduino1.D11_PWM/MOSI, Dot_Matrix1.Row_2
  N5: Arduino1.D12/MISO, Dot_Matrix1.Row_1
  N6: Arduino1.D1/TX, R6.Pin_0
  N7: Arduino1.D2, Dot_Matrix1.Row_3
  N8: Arduino1.D3_PWM, R7.Pin_0
  N9: Arduino1.D4, Dot_Matrix1.Row_5
  N10: Arduino1.D5_PWM, Dot_Matrix1.Row_6
  N11: Arduino1.D6_PWM, Dot_Matrix1.Row_7
  N12: Arduino1.D7, R8.Pin_0
  N13: Arduino1.5V, Q6.E, Q7.E, Q8.E, Q9.E, Q10.E
  N14: Q6.B, R6.Pin_1
  N15: Q6.C, Dot_Matrix1.Column_1
  N16: Q7.B, R7.Pin_1
  N17: Q7.C, Dot_Matrix1.Column_2
  N18: Q8.B, R8.Pin_1
  N19: Q8.C, Dot_Matrix1.Column_4
  N20: Q9.B, R9.Pin_1
  N21: Q9.C, Dot_Matrix1.Column_5
  N22: Q10.B, R10.Pin_1
  N23: Q10.C, Dot_Matrix1.Column_3

notes:
  Sketch by Johannes Findeisen
  www.hanez.org
  Find the Code here:
  Code
