# Fritzing sketch LED-Matrix_simple (saved by Fritzing 0.7.0b)
breadboards: 1

parts:
  Arduino1 = Arduino
  Dot_Matrix = LED Dot Matrix 18mm (0.7 INCH)

nets:
  N1: Arduino1.D12, Dot_Matrix.Row_1
  N2: Arduino1.D11, Dot_Matrix.Row_2
  N3: Arduino1.D10, Dot_Matrix.Column_3
  N4: Arduino1.D9, Dot_Matrix.Row_4
  N5: Arduino1.D8, Dot_Matrix.Column_5
  N6: Arduino1.D7, Dot_Matrix.Column_4
  N7: Arduino1.D6, Dot_Matrix.Row_7
  N8: Arduino1.D5, Dot_Matrix.Row_6
  N9: Arduino1.D4, Dot_Matrix.Row_5
  N10: Arduino1.D3, Dot_Matrix.Column_2
  N11: Arduino1.D2, Dot_Matrix.Row_3
  N12: Arduino1.D1TX, Dot_Matrix.Column_1

notes:
  Sketch by Johannes Findeisen
  www.hanez.org
  Find the Code here:
  Code
