# Fritzing sketch Optocoupler (saved by Fritzing 0.9.10b)
circuit board: 6.88566cm x 5.36311cm
breadboards: 2

parts:
  R3 = Resistor [resistance=220 tolerance=±5% power=0.25 package=THT]
  R4 = Resistor [resistance=220 tolerance=±5% power=0.25 package=THT]
  LED2 = LED - 5mm [color="Red (633nm)" current=0.030 package="5 mm [THT]"]
  VCC1 = Battery
  Arduino2 = Arduino Uno (Rev3)
  U1 = Optocoupler [package=THT]

nets:
  N1: R3.Pin_0, Arduino2.D11_PWM/MOSI
  N2: R3.Pin_1, U1.Pin_1
  N3: R4.Pin_0, LED2.anode
  N4: R4.Pin_1, VCC1.+
  N5: LED2.cathode, U1.Pin_5
  N6: VCC1.-, U1.Pin_4
  N7: Arduino2.GND, U1.Pin_2

notes:
  An optocoupler can be used to control a circuit that's completely isolated from your microcontroller in order to avoid the risk of short-circuit. In this case, imagine that the LED + battery pack combo is a hacked toy that you're turning on and off with the Arduino.
