# Fritzing sketch RGB-LED (saved by Fritzing 0.8.5b)
circuit board: 6.88566cm x 5.36311cm
breadboards: 2

parts:
  Arduino1 = Arduino Uno (Rev3)
  R4 = Resistor [resistance=220 tolerance=±5% package=THT]
  R5 = Resistor [resistance=220 tolerance=±5% package=THT]
  R6 = Resistor [resistance=220 tolerance=±5% package=THT]
  LED = RGB LED (com. cathode, rgb) [package="5 mm [THT]"]

nets:
  N1: Arduino1.D9_PWM, R5.Pin_0
  N2: Arduino1.D10_PWM/SS, R6.Pin_0
  N3: Arduino1.D11_PWM/MOSI, R4.Pin_0
  N4: Arduino1.GND, LED.common_cathode
  N5: R4.Pin_1, LED.red_anode
  N6: R5.Pin_1, LED.blue_anode
  N7: R6.Pin_1, LED.green_anode

notes:
  Let the light shine in any color!
  Check out this forum post for a good code example.
