# Fritzing sketch Relay (saved by Fritzing 0.8.5b)
circuit board: 6.88566cm x 5.36311cm
breadboards: 2

parts:
  Arduino1 = Arduino Uno (Rev3)
  Power_plug2 = Power plug
  M2 = DC Motor
  D3 = Rectifier Diode [part_number=1N4001 package="300 mil [THT]"]
  R4 = Resistor [resistance=1k tolerance=±5% package=THT]
  K2 = Relay [part_number=FRS1B-S package=THT]
  Q3 = NPN-Transistor [package="TO92 [THT]"]

nets:
  N1: Arduino1.GND, Q3.E
  N2: Arduino1.D3_PWM, R4.Pin_1
  N3: Arduino1.5V, D3.cathode, K2.COIL2
  N4: Power_plug2.GND, M2.pin_2
  N5: Power_plug2.VCC, K2.C1, K2.C2
  N6: M2.pin_1, K2.A
  N7: D3.anode, K2.COIL1, Q3.C
  N8: R4.Pin_0, Q3.B

notes:
  In this circuit a 5V relay is connected to the arduino board and controls a DC motor which is connected to an external power supply.
