# Fritzing sketch Sabotage-Detection (saved by Fritzing 0.8.0b)
breadboards: 2

parts:
  Arduino1 = Arduino Uno (Rev3)
  S2 = Pushbutton [package="[THT]"]
  R6 = Resistor [tolerance=±5% resistance=220 package=THT]
  R7 = Resistor [tolerance=±5% resistance=1.1k package=THT]
  R8 = Resistor [tolerance=±5% resistance=220 package=THT]
  R9 = Resistor [tolerance=±5% resistance=220 package=THT]
  LED6 = LED - 5mm [color="Green (555nm)" package="5 mm [THT]"]
  ADXL335 = Triple Axis Accelerometer Breakout - ADXL335
  LED7 = Super Flux LED blue [color=Red]
  LED8 = Super Flux LED blue [color=Blue]
  Pot = Rotary Potentiometer (Small) [maximum_resistance=10kΩ]

nets:
  N1: Arduino1.A0, ADXL335.ZOUT
  N2: Arduino1.A1, ADXL335.YOUT
  N3: Arduino1.A2, ADXL335.XOUT
  N4: Arduino1.A3, Pot.wiper
  GND: Arduino1.GND, R6.Pin_0, R7.Pin_0, R8.Pin_0, R9.Pin_0, ADXL335.GND, Pot.leg2
  N5: Arduino1.D11_PWM/MOSI, LED6.anode
  N6: Arduino1.D2, S2.Pin_3, S2.Pin_4, R7.Pin_1
  N7: Arduino1.D3_PWM, LED7.anode
  N8: Arduino1.D7, LED8.anode
  3V3: Arduino1.3V3, ADXL335.VCC
  N9: Arduino1.5V, S2.Pin_1, S2.Pin_2, Pot.leg1
  N10: R6.Pin_1, LED6.cathode
  N11: R8.Pin_1, LED7.cathode
  N12: R9.Pin_1, LED8.cathode

notes:
  Get the Arduino Code from here:
  Sabotage Alert

// code stored in the sketch: Sabotage-Detection.ino
/*
  _____       .__  __         .__                
_/ ____\______|__|/  |________|__| ____    ____  
\   __\\_  __ \  \   __\___   /  |/    \  / ___\ 
 |  |   |  | \/  ||  |  /    /|  |   |  \/ /_/  >
 |__|   |__|  |__||__| /_____ \__|___|  /\___  / 
                             \/       \//_____/  
  
Example      Sabotage Detection
Autor        Stefan Hermann
Date         5.12.2011

*/

int myState=0;
int greenLedPin=11;
int redLedPin=7;
int blueLedPin=3;
int buttonPin=2;
int potPin=3;
int accZPin=0;
int accYPin=1;
int accXPin=2;

int startAccZ;
int startAccY;
int startAccX;

void setup(){
  pinMode(greenLedPin,OUTPUT);
  pinMode(redLedPin,OUTPUT);
  pinMode(blueLedPin,OUTPUT);
  pinMode(buttonPin,INPUT);
  startAccZ=analogRead(accZPin);
  startAccY=analogRead(accYPin);
  startAccX=analogRead(accXPin);
}

void alertBlinking(){
  digitalWrite(redLedPin,HIGH);
  delay(50);
  digitalWrite(redLedPin,LOW);
  delay(100);
  digitalWrite(blueLedPin,HIGH);
  delay(50);
  digitalWrite(blueLedPin,LOW); 
  delay(100);  
}

boolean senseAcceleration(int myPotVal){
  boolean myReturn=false;
  myPotVal=map(myPotVal,0,1023,0,10);
  if (analogRead(accXPin)>startAccX+myPotVal) myReturn=true;
  if (analogRead(accYPin)>startAccY+myPotVal) myReturn=true;
  if (analogRead(accZPin)>startAccZ+myPotVal) myReturn=true;
  return myReturn;
}

void loop(){
  //alertBlinking();
  switch (myState){
  case 0: //idle
    if (senseAcceleration(analogRead(potPin))==true) {
      digitalWrite(greenLedPin,LOW);
      myState=1;
    } else {
      digitalWrite(greenLedPin,HIGH);    
    };
    break;
  case 1: // alert
    alertBlinking();
    if (digitalRead(buttonPin)==HIGH){
      myState=0;
    }
    break;
  }
  delay(10);
}
