# Fritzing sketch Shift_Register_2x (saved by Fritzing 0.8.5b)
circuit board: 6.88176cm x 9.61717cm
breadboards: 2

parts:
  Arduino1 = Arduino Uno (Rev3)
  R10 = Resistor [resistance=220 tolerance=±5% package=THT]
  R11 = Resistor [resistance=220 tolerance=±5% package=THT]
  R12 = Resistor [resistance=220 tolerance=±5% package=THT]
  R13 = Resistor [resistance=220 tolerance=±5% package=THT]
  R14 = Resistor [resistance=220 tolerance=±5% package=THT]
  R15 = Resistor [resistance=220 tolerance=±5% package=THT]
  R16 = Resistor [resistance=220 tolerance=±5% package=THT]
  R17 = Resistor [resistance=220 tolerance=±5% package=THT]
  LED10 = LED - 5mm [color="Red (633nm)" package="5 mm [THT]"]
  LED11 = LED - 5mm [color="Red (633nm)" package="5 mm [THT]"]
  LED12 = LED - 5mm [color="Red (633nm)" package="5 mm [THT]"]
  LED13 = LED - 5mm [color="Red (633nm)" package="5 mm [THT]"]
  LED14 = LED - 5mm [color="Red (633nm)" package="5 mm [THT]"]
  LED15 = LED - 5mm [color="Red (633nm)" package="5 mm [THT]"]
  LED16 = LED - 5mm [color="Red (633nm)" package="5 mm [THT]"]
  LED17 = LED - 5mm [color="Red (633nm)" package="5 mm [THT]"]
  74HC5952 = 74HC595 [package="DIP16 [THT]"]
  C3 = Ceramic Capacitor [capacitance=100nF rated_voltage=35V package="200 mil [THT, multilayer]"]
  LED18 = LED - 5mm [color="Red (633nm)" package="5 mm [THT]"]
  LED19 = LED - 5mm [color="Red (633nm)" package="5 mm [THT]"]
  LED20 = LED - 5mm [color="Red (633nm)" package="5 mm [THT]"]
  LED21 = LED - 5mm [color="Red (633nm)" package="5 mm [THT]"]
  LED22 = LED - 5mm [color="Red (633nm)" package="5 mm [THT]"]
  LED23 = LED - 5mm [color="Red (633nm)" package="5 mm [THT]"]
  LED24 = LED - 5mm [color="Red (633nm)" package="5 mm [THT]"]
  LED25 = LED - 5mm [color="Red (633nm)" package="5 mm [THT]"]
  R18 = Resistor [resistance=220 tolerance=±5% package=THT]
  R19 = Resistor [resistance=220 tolerance=±5% package=THT]
  R20 = Resistor [resistance=220 tolerance=±5% package=THT]
  R21 = Resistor [resistance=220 tolerance=±5% package=THT]
  R22 = Resistor [resistance=220 tolerance=±5% package=THT]
  R23 = Resistor [resistance=220 tolerance=±5% package=THT]
  R24 = Resistor [resistance=220 tolerance=±5% package=THT]
  R25 = Resistor [resistance=220 tolerance=±5% package=THT]
  74HC5953 = 74HC595 [package="DIP16 [THT]"]

nets:
  GND: Arduino1.GND, LED10.cathode, LED11.cathode, LED12.cathode, LED13.cathode, LED14.cathode, LED15.cathode, LED16.cathode, LED17.cathode, 74HC5952.GND, 74HC5952.OE, C3.1, LED18.cathode, LED19.cathode, LED20.cathode, LED21.cathode, LED22.cathode, LED23.cathode, LED24.cathode, LED25.cathode, 74HC5953.GND, 74HC5953.OE
  VCC: Arduino1.5V, 74HC5952.MR, 74HC5952.VCC, 74HC5953.MR, 74HC5953.VCC
  N1: Arduino1.D8, 74HC5952.ST_CP, C3.0, 74HC5953.ST_CP
  N2: Arduino1.D11_PWM/MOSI, 74HC5952.DS, 74HC5953.Q7'
  N3: Arduino1.D12/MISO, 74HC5952.SH_CP, 74HC5953.SH_CP
  N4: R10.Pin_0, LED14.anode
  N5: R10.Pin_1, 74HC5952.Q6
  N6: R11.Pin_0, LED10.anode
  N7: R11.Pin_1, 74HC5952.Q5
  N8: R12.Pin_0, LED12.anode
  N9: R12.Pin_1, 74HC5952.Q4
  N10: R13.Pin_0, LED11.anode
  N11: R13.Pin_1, 74HC5952.Q7
  N12: R14.Pin_0, LED13.anode
  N13: R14.Pin_1, 74HC5952.Q3
  N14: R15.Pin_0, LED15.anode
  N15: R15.Pin_1, 74HC5952.Q2
  N16: R16.Pin_0, LED16.anode
  N17: R16.Pin_1, 74HC5952.Q1
  N18: R17.Pin_0, LED17.anode
  N19: R17.Pin_1, 74HC5952.Q0
  N20: LED18.anode, R19.Pin_0
  N21: LED19.anode, R21.Pin_0
  N22: LED20.anode, R20.Pin_0
  N23: LED21.anode, R22.Pin_0
  N24: LED22.anode, R18.Pin_0
  N25: LED23.anode, R23.Pin_0
  N26: LED24.anode, R24.Pin_0
  N27: LED25.anode, R25.Pin_0
  N28: R18.Pin_1, 74HC5953.Q6
  N29: R19.Pin_1, 74HC5953.Q5
  N30: R20.Pin_1, 74HC5953.Q4
  N31: R21.Pin_1, 74HC5953.Q7
  N32: R22.Pin_1, 74HC5953.Q3
  N33: R23.Pin_1, 74HC5953.Q2
  N34: R24.Pin_1, 74HC5953.Q1
  N35: R25.Pin_1, 74HC5953.Q0

notes:
  In this project, two 74HC595 shift register are used to control 16 LEDs with just 3 Arduino pins.
  Related example: http://www.arduino.cc/en/Tutorial/ShiftOut
