# Fritzing sketch TemperaturSensorLM35 (saved by Fritzing 0.8.6b)
circuit board: 6.88566cm x 5.36311cm
breadboards: 2

parts:
  T2 = LM35 Temperature Sensor [package="TO92 [THT]"]
  R7 = Resistor [tolerance=±5% resistance=220 package=THT]
  R8 = Resistor [tolerance=±5% resistance=220 package=THT]
  R9 = Resistor [tolerance=±5% resistance=220 package=THT]
  R10 = Resistor [tolerance=±5% resistance=220 package=THT]
  R11 = Resistor [tolerance=±5% resistance=220 package=THT]
  LED7 = LED - 5mm [color="Red (633nm)" package="5 mm [THT]"]
  LED8 = LED - 5mm [color="Red (633nm)" package="5 mm [THT]"]
  LED9 = LED - 5mm [color="Yellow (595nm)" package="5 mm [THT]"]
  LED10 = LED - 5mm [color="Yellow (595nm)" package="5 mm [THT]"]
  LED11 = LED - 5mm [color="Green (555nm)" package="5 mm [THT]"]
  LED12 = LED - 5mm [color="Green (555nm)" package="5 mm [THT]"]
  R12 = Resistor [tolerance=±5% resistance=220 package=THT]
  Arduino1 = Arduino Uno (Rev3)
  part = Resistor [tolerance=±5% resistance=220 package=THT]  # not connected

nets:
  N1: T2.+Vs, Arduino1.5V
  N2: T2.Vout, Arduino1.A0
  GND: T2.GND, R7.Pin_0, R8.Pin_0, R9.Pin_0, R10.Pin_0, R11.Pin_0, R12.Pin_0, Arduino1.GND
  N3: R7.Pin_1, LED7.anode
  N4: R8.Pin_1, LED8.anode
  N5: R9.Pin_1, LED9.anode
  N6: R10.Pin_1, LED10.anode
  N7: R11.Pin_1, LED11.anode
  N8: LED7.cathode, Arduino1.D7
  N9: LED8.cathode, Arduino1.D6_PWM
  N10: LED9.cathode, Arduino1.D5_PWM
  N11: LED10.cathode, Arduino1.D4
  N12: LED11.cathode, Arduino1.D3_PWM
  N13: LED12.cathode, Arduino1.D2
  N14: LED12.anode, R12.Pin_1

notes:
  Digital Thermometer
  get the code from here
  Digital Thermometer with LM35
