# Fritzing sketch TiltSwitch (saved by Fritzing 0.8.6b)
circuit board: 6.88566cm x 5.36311cm
breadboards: 2

parts:
  Switch = Tilt Switch [package=THT]
  R1 = Resistor [tolerance=±5% resistance=100k package=THT]
  Arduino1 = Arduino Uno (Rev3)
  part = Resistor [tolerance=±5% resistance=220 package=THT]  # not connected

nets:
  N1: Switch.Pin_1, R1.Pin_1, Arduino1.D2
  N2: Switch.Pin_2, Arduino1.5V
  N3: R1.Pin_0, Arduino1.GND

notes:
  In this example, a tilt switch is used (just like a button) as a digital input, and an LED is a digital output. The resistor is a pull-down resistor.
  Related example: http://www.arduino.cc/en/Tutorial/TiltSensor
