# Fritzing sketch Timer (saved by Fritzing 0.8.6b)
circuit board: 6.88566cm x 5.36311cm
breadboards: 2

parts:
  7_Segment1 = 7 Segment Display
  S2 = Pushbutton [package="[THT]"]
  S1 = Pushbutton [package="[THT]"]
  R2 = Resistor [resistance=10k tolerance=±5% package=THT]
  7_Segment2 = 7 Segment Display
  R30 = Resistor [resistance=220 tolerance=±5% package=THT]
  R31 = Resistor [resistance=220 tolerance=±5% package=THT]
  R32 = Resistor [resistance=220 tolerance=±5% package=THT]
  R36 = Resistor [resistance=220 tolerance=±5% package=THT]
  R37 = Resistor [resistance=220 tolerance=±5% package=THT]
  R38 = Resistor [resistance=220 tolerance=±5% package=THT]
  R39 = Resistor [resistance=220 tolerance=±5% package=THT]
  R40 = Resistor [resistance=220 tolerance=±5% package=THT]
  R41 = Resistor [resistance=220 tolerance=±5% package=THT]
  R42 = Resistor [resistance=220 tolerance=±5% package=THT]
  R43 = Resistor [resistance=220 tolerance=±5% package=THT]
  R44 = Resistor [resistance=220 tolerance=±5% package=THT]
  R45 = Resistor [resistance=220 tolerance=±5% package=THT]
  R46 = Resistor [resistance=220 tolerance=±5% package=THT]
  R1 = Resistor [resistance=10k tolerance=±5% package=THT]
  IC1 = IC, DIP package, 16 pins [chip_label=595]
  IC2 = IC, DIP package, 16 pins [chip_label=595]
  Arduino1 = Arduino Uno (Rev3)

nets:
  N1: 7_Segment1.Segment_E, R45.Pin_1
  N2: 7_Segment1.Segment_D, R42.Pin_0
  N3: 7_Segment1.common_anode, S2.Pin_3, S2.Pin_4, S1.Pin_3, S1.Pin_4, 7_Segment2.common_anode, IC1.pin10, IC1.pin16, IC2.pin10, IC2.pin16, Arduino1.5V
  N4: 7_Segment1.Segment_C, R41.Pin_0
  N5: 7_Segment1.Segment_B, R40.Pin_0
  N6: 7_Segment1.Segment_A, R43.Pin_0
  N7: 7_Segment1.Segment_F, R39.Pin_1
  N8: 7_Segment1.Segment_G, R38.Pin_1
  N9: S2.Pin_1, S2.Pin_2, R2.Pin_0, Arduino1.D5_PWM
  N10: S1.Pin_1, S1.Pin_2, R1.Pin_0, Arduino1.D6_PWM
  N11: R2.Pin_1, R1.Pin_1, IC1.pin8, IC1.pin13, IC2.pin8, IC2.pin13, Arduino1.GND
  N12: 7_Segment2.Segment_E, R46.Pin_1
  N13: 7_Segment2.Segment_D, R37.Pin_0
  N14: 7_Segment2.Segment_C, R36.Pin_0
  N15: 7_Segment2.Segment_B, R32.Pin_0
  N16: 7_Segment2.Segment_A, R44.Pin_0
  N17: 7_Segment2.Segment_F, R31.Pin_1
  N18: 7_Segment2.Segment_G, R30.Pin_1
  N19: R30.Pin_0, IC2.pin6
  N20: R31.Pin_0, IC2.pin5
  N21: R32.Pin_1, IC2.pin1
  N22: R36.Pin_1, IC2.pin2
  N23: R37.Pin_1, IC2.pin3
  N24: R38.Pin_0, IC1.pin6
  N25: R39.Pin_0, IC1.pin5
  N26: R40.Pin_1, IC1.pin1
  N27: R41.Pin_1, IC1.pin2
  N28: R42.Pin_1, IC1.pin3
  N29: R43.Pin_1, IC1.pin15
  N30: R44.Pin_1, IC2.pin15
  N31: R45.Pin_0, IC1.pin4
  N32: R46.Pin_0, IC2.pin4
  N33: IC1.pin9, IC2.pin14
  N34: IC1.pin11, IC2.pin11, Arduino1.D12/MISO
  N35: IC1.pin12, IC2.pin12, Arduino1.D8
  N36: IC1.pin14, Arduino1.D11_PWM/MOSI

notes:
  Example from Frerk Popovic
  www.popovic.info
