# Fritzing sketch VirtualColorMixer (saved by Fritzing 0.7.0b)
breadboards: 1

parts:
  R3 = Rotary Potentiometer (Large) [maximum_resistance=100kΩ package=THT]
  R1 = Rotary Potentiometer (Large) [maximum_resistance=100kΩ package=THT]
  R2 = Rotary Potentiometer (Large) [maximum_resistance=100kΩ package=THT]
  Arduino1 = Arduino

nets:
  N1: R3.leg1, R1.leg1, R2.leg1, Arduino1.+5V
  N2: R3.wiper, Arduino1.A2
  N3: R3.leg2, R1.leg2, R2.leg2, Arduino1.GND
  N4: R1.wiper, Arduino1.A0
  N5: R2.wiper, Arduino1.A1

notes:
  You can send multiple values from the Arduino board to the computer using the serial print function. In this project, the analog values from three potentiometers are used to set the red, green, and blue values of the background color of a Processing sketch running on the computer.
  http://arduino.cc/en/Tutorial/VirtualColorMixer
