# Fritzing sketch Window_Alarm (saved by Fritzing 0.8.5b)
circuit board: 6.88566cm x 5.36311cm
breadboards: 2

parts:
  Arduino1 = Arduino Uno (Rev3)
  Speaker1 = Piezo Speaker
  R3 = Resistor [resistance=10k tolerance=±5% package=THT]
  Reed_Switch1 = Reed switch [package=THT]

nets:
  N1: Arduino1.GND, Speaker1.pin1, R3.Pin_1
  N2: Arduino1.D9_PWM, Speaker1.pin2
  N3: Arduino1.D12/MISO, R3.Pin_0, Reed_Switch1.pin_1
  N4: Arduino1.5V, Reed_Switch1.pin_2

notes:
  Reed switches close when a magnet is placed near their casing. In this example, a magnet could be mounted on a window and the reed switch on the windowsill so that everytime the window was opened, the piezo buzzer would sound.
  http://arduino.cc/en/Tutorial/Button
  http://arduino.cc/en/Tutorial/Melody
